# Fritzing sketch MTI Final (saved by Fritzing 0.9.10b)
breadboards: 1

parts:
  Gyro = MPU-6050 Board GY-521 [form="♀ (female)" package=THT]
  Part1 = Arduino Uno (Rev3) - ICSP
  R1 = Resistor [tolerance=±5% resistance=1M package="0603 [SMD]"]
  24_LEDs_Ring = 24 NeoPixel Ring [part_number=1643]

nets:
  5V: Gyro.pin1, Part1.5V, 24_LEDs_Ring.VDD
  GND: Gyro.pin2, Part1.GND, 24_LEDs_Ring.GND
  N1: Gyro.pin3, Part1.A5/SCL
  N2: Gyro.pin4, Part1.A4/SDA
  N3: Part1.D8, R1.Pin_0
  N4: Part1.D9_PWM, 24_LEDs_Ring.IN
  N5: Part1.D7, R1.Pin_1

custom parts:
  MPU-6050 Board GY-521: Acelerometro y Giroscopio MPU-6050 Board GY-521
  24 NeoPixel Ring: 24 ultra bright smart LED NeoPixels are arranged in a circle with 1.5" (37mm) outer diameter. The rings are 'chainable' - connect the output pin of one to the input pin of another. Use only one microcontroller pin to control as many as you can chain together! Each LED is addressable as the driver chip is inside the LED. Each one has ~18mA constant current drive so the color will be very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
